# Fritzing sketch layout (saved by Fritzing 0.6.5b)
breadboards: 1

parts:
  Arduino1 = Arduino
  J1 = Piezo Speaker
  S1 = Pushbutton [package="[THT]"]
  LED1 = LED - 5mm [color="Green (555nm)" package="5 mm [THT]"]
  R1 = Resistor [tolerance=±5% resistance=10k package=THT]
  R2 = Resistor [tolerance=±5% resistance=220 package=THT]  # not connected
  R3 = Resistor [tolerance=±5% resistance=10 package=THT]

nets:
  N1: Arduino1.GND, R1.Pin_1
  N2: Arduino1.D2, S1.Pin_1, S1.Pin_2, R1.Pin_0
  N3: Arduino1.+5V, J1.pin1, LED1.cathode
  N4: J1.pin2, R3.Pin_0
  N5: S1.Pin_3, S1.Pin_4
